# Fritzing sketch Schematics NODE New (saved by Fritzing 0.9.3b)
breadboards: 1

parts:
  Part4 = Arduino Uno (Rev3)
  RHT2 = Humidity and Temperature Sensor RHT03
  R1 = Resistor [tolerance=±5% resistance=220 package="0402 [SMD]"]
  R2 = PHOTOCELL [package=photocell-kit]
  R3 = Resistor [tolerance=±5% resistance=10k package=THT]
  LCD1 = LCD screen  # not connected

nets:
  N1: Part4.A0, R2.P$2, R3.Pin_0
  N2: Part4.D2, RHT2.Data-signal, R1.Pin_0
  5V: Part4.5V, RHT2.Vcc, R1.Pin_1, R2.P$1
  N3: Part4.GND, RHT2.GND_2, R3.Pin_1

notes:
  [ The LCD Display was connected to the ARDUINO-UNO but We did not see the 12c Module required for the connection.]

// code stored in the sketch: Breadboard NODE.ino

