# Fritzing sketch Breadboard SERVER (saved by Fritzing 0.9.3b)
breadboards: 1

parts:
  Part1 = Arduino Mega ADK (Rev3)
  LCD1 = LCD screen  # not connected
  Part3 = TRRS 3.5mm Jack Breakout
  IC1 = DS1302 [package="DIP8 [THT]"]
  IR1 = TSOP312.., 314.. [package=THT]

nets:
  N1: Part1.A0, IC1.X1_-_Crystal
  N2: Part1.A1, IC1.X2_-_Crystal
  N3: Part1.A2, IC1.CE_-_Chip_Enable
  N4: Part1.D19/RX1, Part3.TIP
  N5: Part1.D18/TX1, Part3.RING1
  N6: Part1.IOREF, Part1.5V, Part3.SLEEVE, IC1.0V, IR1.Data
  N7: Part1.GND, Part3.RING2, IC1.+V, IC1.Vbat_-_Backup_Supply, IR1.Vs
  N8: Part1.D22, IR1.GND

notes:
  [non-connected DS1302 is for the battery]
  [ The LCD Disploay was connected to the ARDUINO-MEGA but We did not see the 12c Module required for the connection.]
